# Fritzing sketch pump_controller_mosfet_max_pressure-3 (saved by Fritzing 0.9.9b)
breadboards: 2

parts:
  Part1 = Arduino Uno (Rev3)
  Q1 = Basic FET P-Channel [package="TO220 [THT]"]
  R1 = Resistor [tolerance=±5% power=0.25 resistance=10k package=THT]
  D1 = Rectifier Diode [part_number=1N4001 package="300 mil [THT]"]
  Duty_Cycle = Trimmer Potentiometer [maximum_resistance=10kΩ package=THT]
  Part2 = DC Voltage Source 12V [package=THT]
  R6 = Trimmer Potentiometer [maximum_resistance=10kΩ package=THT]
  Q3 = PNP-Transistor [package="TO92 [THT]"]
  UV = Super Flux LED blue [color=Blue]
  Part3 = DC Voltage Source 5V [package=THT]
  LED1 = LED - 5mm [color="Green (555nm)" current=0.030 package="5 mm [THT]"]
  R7 = Resistor [tolerance=±5% power=0.25 resistance=680 package=THT]
  S1 = Taiway 100-SP-X-T1 SPDT Miniature Toggle Switch [part_number=100-SP-X-T1-0-0-B1-M2 package=THT]
  S3 = Taiway 100-SP-X-T1 SPDT Miniature Toggle Switch [part_number=100-SP-X-T1-0-0-B1-M2 package=THT]
  R8 = Resistor [tolerance=±5% power=0.25 resistance=10k package=THT]
  Pump = DC Motor
  U1 = attiny85 [package=dip]
  U2 = Optocoupler [package=THT]
  R9 = Resistor [tolerance=±5% power=0.25 resistance=680 package=THT]  # not connected
  R10 = Resistor [tolerance=±5% power=0.25 resistance=1k package=THT]
  R11 = Resistor [tolerance=±5% power=0.25 resistance=1k package=THT]

nets:
  N1: Part1.A4/SDA, Q3.B
  N2: Part1.D11_PWM/MOSI, Q1.gate, R1.Pin_1, U1.Pin_6
  N3: Part1.D12/MISO, S3.COM, R8.Pin_0, U1.Pin_5
  N4: Part1.GND, Q1.source, R1.Pin_0, Duty_Cycle.leg1, Part2.V–, R6.leg1, Q3.C, UV.cathode, Part3.V–, S3.L1, U1.Pin_4, U2.Pin_4, R11.Pin_1
  N5: Q1.drain, D1.anode, LED1.anode, Pump.pin_2
  N6: D1.cathode, UV.anode, Part3.V+#0, R7.Pin_1, S1.L1, Pump.pin_1
  N7: Duty_Cycle.leg2, R6.leg2, Q3.E, Part3.V+#2, R8.Pin_1, U1.Pin_8, R10.Pin_0
  N8: Part2.V+, S1.COM
  N9: LED1.cathode, R7.Pin_0
  N10: U2.Pin_1, R10.Pin_1
  N11: U2.Pin_5, R11.Pin_0

notes:
  Actual Pressure
  Target Pressure
  Flow (Duty Cycle )
  12V
  Pullup: LOW = Continuous
  Main ON-OFF
  - CONTINUOUS ON
  - PRESSURE-DRIVEN

custom parts:
  DC Voltage Source 5V: A dummy, proxy, ersatz, stand-in part for whatever you want. With 3 pins on a 100 mil inline pin header footprint.
