# Fritzing sketch pump_controller_mosfet_max_pressure_uno (saved by Fritzing 0.9.9b)
breadboards: 2

parts:
  Part1 = Arduino Uno (Rev3)
  Q1 = Basic FET P-Channel [package="TO220 [THT]"]
  R1 = Resistor [tolerance=±5% power=0.25 resistance=4.7k package=THT]
  D1 = Rectifier Diode [part_number=1N4001 package="300 mil [THT]"]
  Pump = Solenoid
  Duty_Cycle = Trimmer Potentiometer [maximum_resistance=10kΩ package=THT]
  Part2 = DC Voltage Source 12V [package=THT]
  R6 = Trimmer Potentiometer [maximum_resistance=10kΩ package=THT]
  Q3 = PNP-Transistor [package="TO92 [THT]"]
  UV = Super Flux LED blue [color=Blue]
  Tap_1 = Momentary Switch [package=ksa_sealed_tac_switch]
  Tap_2 = Momentary Switch [package=ksa_sealed_tac_switch]
  Part3 = DC Voltage Source 5V [package=THT]
  LED1 = LED - 5mm [color="Green (555nm)" current=0.030 package="5 mm [THT]"]
  R7 = Resistor [tolerance=±5% power=0.25 resistance=680 package=THT]
  R8 = Resistor [tolerance=±5% resistance=10k package="0402 [SMD]"]
  S1 = Taiway 100-SP-X-T1 SPDT Miniature Toggle Switch [part_number=100-SP-X-T1-0-0-B1-M2 package=THT]
  S2 = Taiway 100-SP-X-T1 SPDT Miniature Toggle Switch [part_number=100-SP-X-T1-0-0-B1-M2 package=THT]
  D2 = Rectifier Diode [part_number=1N4001 package="300 mil [THT]"]

nets:
  N1: Part1.A0, Q3.E
  N2: Part1.A1, R6.wiper
  N3: Part1.A2, Duty_Cycle.wiper
  N4: Part1.D6_PWM, Q1.gate, R1.Pin_1, R8.Pin_0
  GND: Part1.GND, Part1.VIN, Q1.source, R1.Pin_0, D1.cathode, Pump.pin2, Duty_Cycle.leg1, Part2.V–#4, R6.leg1, Q3.C, UV.anode, Tap_1.1, Tap_1.2, Tap_2.1, Tap_2.2, Part3.V+#0, Part3.V–#4, R7.Pin_1, S1.L2, S2.L1, D2.anode
  N5: Q1.drain, D1.anode, Pump.pin1, LED1.anode
  N6: Duty_Cycle.leg2, R6.leg2, Q3.B, Part3.V+#2
  N7: Part2.V–#1, Part3.V–#1
  N8: Part2.V+, S1.L1
  N9: UV.cathode, R8.Pin_1, S2.L2, D2.cathode
  N10: Tap_1.3, Tap_1.4
  N11: Tap_2.3, Tap_2.4
  N12: LED1.cathode, R7.Pin_0

notes:
  Actual Pressure
  Target Pressure
  Flow (Duty Cycle )
  Tap / Pressure
  Off
  On
  12V

custom parts:
  DC Voltage Source 5V: A dummy, proxy, ersatz, stand-in part for whatever you want. With 3 pins on a 100 mil inline pin header footprint.
